# Fritzing sketch pico_breadboard (saved by Fritzing 0.9.3b)
breadboards: 1

parts:
  Mod1 = Raspberry Pi Pico
  J1 = Basic Servo
  J2 = Basic Servo
  S1 = Pushbutton [package="[THT]"]

nets:
  GND: Mod1.pin_3, Mod1.pin_8, Mod1.pin_13, Mod1.pin_18, Mod1.pin_23, Mod1.pin_28, Mod1.pin_33, Mod1.pin_38, J1.gnd, J2.gnd
  N1: Mod1.pin_4, J1.pulse
  N2: Mod1.pin_5, J2.pulse
  N3: Mod1.pin_30, S1.Pin_1, S1.Pin_2, S1.Pin_3
  N4: Mod1.pin_40, J2.vcc

notes:
  Serial to Pi GPIO 14,15
  5v rail
  Upper/tilt
  Lower/pan

custom parts:
  Raspberry Pi Pico: Raspberry Pi Pico. Based around the RP2040 microcontroller the Pico is a low cost microcontroller device bringing Raspberry Pi quality, cost, and easy of use to the microcontroller space. Jan 2021, Split part in to two versions: tht (this one) and SMD. This one will drill holes for a .1 in header in pcb to allow plugging in the module as well as providing pads to solder the module to the top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
